// Logisim project Control_Unit_Final.circ as structural Verilog: 2 circuits, main circuit main
// Control Unit
module main (
  input  [5:0] OP6,
  output out_2,
  output out_3,
  output out_4,
  output out_5,
  output out_6,
  output out_7,
  output out_8,
  output out_9
);

  J_Branch j_branch_1 (._6_bit_Op(OP6), .Jump(out_2));  // open: Branch
  Op_Control op_control_1 (.ExtOp(out_8), .ALUSrc(out_9), ._6_bit_Op(OP6));
  Storage_Control_Unit storage_control_unit_1 (
    .RegSrc(out_3), .RegWr(out_4), .MemRd(out_5), .MemWr(out_6), .MemtoReg(out_7), .in_1(OP6));
endmodule

module f (
);

  main main_1 ();  // open: OP6, out_2, out_3, out_4, out_5, out_6, out_7, out_8, out_9
endmodule
