// Logisim project Extender.circ as structural Verilog: 1 circuit, main circuit Extender
module Extender (
  input  [15:0] Immediate,
  input  Extender_Op,
  output [31:0] Immediate_2
);

  wire [31:0] bit_extender_1_out, bit_extender_2_out;

  assign bit_extender_1_out = {{16{1'b0}}, Immediate};  // Bit_Extender bit_extender_1
  assign bit_extender_2_out = {{16{Immediate[15]}}, Immediate};  // Bit_Extender bit_extender_2
  Multiplexer #(.width(32)) multiplexer_1 (
    .in0(bit_extender_1_out), .in1(bit_extender_2_out), .out(Immediate_2), .sel(Extender_Op));  // open: en
endmodule
