// Logisim project Hazard Detect Forward and Stall.circ as structural Verilog: 3 circuits, main circuit FarwardA
module FarwardA (
  input  [31:0] Rs,
  input  [31:0] EX_Rd,
  input  EX_RegWr,
  input  [31:0] MEM_Rd,
  input  MEM_RegWr,
  input  [31:0] WB_Rd,
  input  WE_RegWr,
  output [1:0] ForwardA
);

  wire and_1_out, and_2_out, and_3_out, and_4_out, and_5_out, and_6_out, comparator_1_eq, comparator_2_eq,
       comparator_3_eq, not_1_out, not_2_out, not_3_out;

  Comparator #(.width(32)) comparator_1 (.a(Rs), .b(EX_Rd), .eq(comparator_1_eq));  // open: gt, lt
  Comparator #(.width(32)) comparator_2 (.a(Rs), .b(MEM_Rd), .eq(comparator_2_eq));  // open: gt, lt
  Comparator #(.width(32)) comparator_3 (.a(Rs), .b(WB_Rd), .eq(comparator_3_eq));  // open: gt, lt
  and and_1 (and_1_out, comparator_1_eq, EX_RegWr);
  and and_2 (and_2_out, comparator_2_eq, MEM_RegWr);
  and and_3 (and_3_out, comparator_3_eq, WE_RegWr);
  not not_1 (not_1_out, and_1_out);
  not not_2 (not_2_out, and_1_out);
  not not_3 (not_3_out, and_2_out);
  and and_4 (and_4_out, not_1_out, and_3_out);
  and and_5 (and_5_out, not_2_out, and_2_out);
  and and_6 (and_6_out, not_3_out, and_3_out);
  or or_1 (ForwardA[0], and_4_out, and_5_out);
  or or_2 (ForwardA[1], and_6_out, and_1_out);
endmodule

module ForwardB (
  input  [31:0] Rt,
  input  [31:0] EX_Rd,
  input  EX_RegWr,
  input  [31:0] MEM_Rd,
  input  MEM_RegWr,
  input  [31:0] WB_Rd,
  input  WE_RegWr,
  output [1:0] ForwardB
);

  wire and_1_out, and_2_out, and_3_out, and_4_out, and_5_out, and_6_out, comparator_1_eq, comparator_2_eq,
       comparator_3_eq, not_1_out, not_2_out, not_3_out;

  Comparator #(.width(32)) comparator_1 (.a(Rt), .b(EX_Rd), .eq(comparator_1_eq));  // open: gt, lt
  Comparator #(.width(32)) comparator_2 (.a(Rt), .b(MEM_Rd), .eq(comparator_2_eq));  // open: gt, lt
  Comparator #(.width(32)) comparator_3 (.a(Rt), .b(WB_Rd), .eq(comparator_3_eq));  // open: gt, lt
  and and_1 (and_1_out, comparator_1_eq, EX_RegWr);
  and and_2 (and_2_out, comparator_2_eq, MEM_RegWr);
  and and_3 (and_3_out, comparator_3_eq, WE_RegWr);
  not not_1 (not_1_out, and_1_out);
  not not_2 (not_2_out, and_1_out);
  not not_3 (not_3_out, and_2_out);
  and and_4 (and_4_out, not_1_out, and_3_out);
  and and_5 (and_5_out, not_2_out, and_2_out);
  and and_6 (and_6_out, not_3_out, and_3_out);
  or or_1 (ForwardB[0], and_4_out, and_5_out);
  or or_2 (ForwardB[1], and_6_out, and_1_out);
endmodule

module Hazard_Detect_Forward_and_Stall (
  input  [4:0] Rs,
  input  [4:0] Rd_EX,
  input  RegWr_EX,
  input  [4:0] Rd_MEM,
  input  RegWr_MEM,
  input  [4:0] Rd_WB,
  input  RegWr_WB,
  input  [4:0] Rt,
  input  MemRd_EX,
  output [1:0] ForwardA,
  output [1:0] ForwardB,
  output Stall
);

  wire and_1_out, and_2_out, and_3_out, and_4_out, and_5_out, and_6_out, and_7_out, and_8_out, and_9_out,
       and_10_out, and_11_out, and_12_out, and_13_out, and_14_out, comparator_1_eq, comparator_2_eq,
       comparator_3_eq, comparator_4_eq, comparator_5_eq, comparator_6_eq, not_1_out, not_2_out, not_3_out,
       not_4_out, not_5_out, not_6_out, not_7_out, not_8_out, not_9_out, not_10_out, not_11_out, not_12_out,
       or_5_out;

  Comparator #(.width(5)) comparator_1 (.a(Rs), .b(Rd_EX), .eq(comparator_1_eq));  // open: gt, lt
  Comparator #(.width(5)) comparator_2 (.a(Rs), .b(Rd_MEM), .eq(comparator_2_eq));  // open: gt, lt
  Comparator #(.width(5)) comparator_3 (.a(Rs), .b(Rd_WB), .eq(comparator_3_eq));  // open: gt, lt
  Comparator #(.width(5)) comparator_4 (.a(Rt), .b(Rd_EX), .eq(comparator_4_eq));  // open: gt, lt
  Comparator #(.width(5)) comparator_5 (.a(Rt), .b(Rd_MEM), .eq(comparator_5_eq));  // open: gt, lt
  Comparator #(.width(5)) comparator_6 (.a(Rt), .b(Rd_WB), .eq(comparator_6_eq));  // open: gt, lt
  and and_1 (and_1_out, comparator_1_eq, RegWr_EX);
  and and_2 (and_2_out, comparator_2_eq, RegWr_MEM);
  and and_3 (and_3_out, comparator_3_eq, RegWr_WB);
  and and_4 (and_4_out, comparator_4_eq, RegWr_EX);
  and and_5 (and_5_out, comparator_5_eq, RegWr_MEM);
  and and_6 (and_6_out, comparator_6_eq, RegWr_WB);
  not not_1 (not_1_out, and_1_out);
  not not_2 (not_2_out, and_2_out);
  not not_3 (not_3_out, and_1_out);
  not not_4 (not_4_out, and_1_out);
  not not_5 (not_5_out, and_2_out);
  not not_6 (not_6_out, and_4_out);
  not not_7 (not_7_out, and_5_out);
  not not_8 (not_8_out, and_4_out);
  not not_9 (not_9_out, and_4_out);
  not not_10 (not_10_out, and_5_out);
  and and_7 (and_7_out, not_1_out, not_2_out, and_3_out);
  and and_8 (and_8_out, not_3_out, and_2_out);
  and and_9 (and_9_out, not_4_out, not_5_out, and_3_out);
  and and_10 (and_10_out, not_6_out, not_7_out, and_6_out);
  and and_11 (and_11_out, not_8_out, and_5_out);
  and and_12 (and_12_out, not_9_out, not_10_out, and_6_out);
  or or_1 (ForwardA[0], and_1_out, and_7_out);
  or or_2 (ForwardA[1], and_8_out, and_9_out);
  or or_3 (ForwardB[0], and_4_out, and_10_out);
  or or_4 (ForwardB[1], and_11_out, and_12_out);
  and and_13 (and_13_out, ForwardB[0], not_11_out);
  not not_11 (not_11_out, ForwardB[1]);
  and and_14 (and_14_out, ForwardA[0], not_12_out);
  not not_12 (not_12_out, ForwardA[1]);
  or or_5 (or_5_out, and_13_out, and_14_out);
  and and_15 (Stall, or_5_out, MemRd_EX);
endmodule
