// Logisim project Instruction_Memory.circ as structural Verilog: 1 circuit, main circuit Instruction Memory
module Instruction_Memory (
  input  [19:0] PC,
  input  [31:0] Input_Data,
  input  Clk,
  output [31:0] _32_bit_iinstruction
);

  RAM #(.addrWidth(20), .dataWidth(32), .bus("separate")) ram_1 (
    .addr(PC), .din(Input_Data), .data(_32_bit_iinstruction), .str(1'b0), .clk(Clk), .ld(1'b1));  // open: sel, clr

  // Notes on the sheet:
  //   SB_Type
  //   R_Tube
  //   INSTRUCTION MEMORY
  //   I-Type
endmodule
