// Logisim project PC counter.circ as structural Verilog: 3 circuits, main circuit PC+1
module PC_1 (
  input  [19:0] Initial_Pc,
  output [19:0] OutPcPlus1
);

  Adder #(.width(20)) adder_1 (.a(Initial_Pc), .b(20'h1), .out(OutPcPlus1), .cin(1'b0));  // open: cout
endmodule

// Jump Unit
module Jump (
  input  [19:0] initial_pc,
  input  [15:0] Imm16,
  input  [31:0] Rs1,
  output [19:0] Pc_jump
);

  wire [19:0] bit_extender_1_out;

  assign bit_extender_1_out = {{4{1'b0}}, Imm16};  // Bit_Extender bit_extender_1
  Adder #(.width(20)) adder_1 (.a(bit_extender_1_out), .b(Rs1[19:0]), .out(Pc_jump), .cin(1'b0));  // open: cout

  // Notes on the sheet:
  //   JALR Rd,Rs1,imm16
endmodule

// Branch Unit
module Branch_pc (
  input  [4:0] ImmL,
  input  [10:0] ImmU,
  input  [19:0] initial_pc,
  output [19:0] Pc_Branch
);

  wire [19:0] bit_extender_1_out;

  assign bit_extender_1_out = {{4{1'b0}}, {ImmU, ImmL}};  // Bit_Extender bit_extender_1
  Adder #(.width(20)) adder_1 (.a(initial_pc), .b(bit_extender_1_out), .out(Pc_Branch), .cin(1'b0));  // open: cout
endmodule
